# Fritzing sketch Untitled Sketch (saved by Fritzing 0.9.3b)
breadboards: 1

parts:
  S1 = Pushbutton [package="[THT]"]
  R1 = Resistor [tolerance=±5% resistance=220 package=THT]
  C1 = Capacitor [package=cap-pth-small2]

nets:
  N1: S1.Pin_1, S1.Pin_2, C1.2
  N2: S1.Pin_3, S1.Pin_4, R1.Pin_1, C1.1
